// Logisim project DuploFlipFlopTipoDTTl7474_2.circ as structural Verilog: 1 circuit, main circuit main
module main (
);

  wire n7474_1_pin1, n7474_1_pin2, n7474_1_pin3, n7474_1_pin5, n7474_2_pin1, n7474_2_pin2, n7474_2_pin3,
       n7474_2_pin5, n7474_2_pin9, n7474_2_pin12;

  _7_Segment_Display u_7_segment_display_1 ();  // open: g, f, a, b, e, d, c, dp
  _7474 u_7474_1 (
    .pin1(n7474_1_pin1), .pin2(n7474_1_pin2), .pin3(n7474_1_pin3), .pin4(n7474_1_pin1), .pin5(n7474_1_pin5),
    .pin6(n7474_1_pin2));  // open: pin13, pin12, pin11, pin10, pin9, pin8
  Button button_1 (.out(n7474_1_pin3));
  LED led_1 (.in(n7474_1_pin5));
  _7474 u_7474_2 (
    .pin1(n7474_2_pin1), .pin2(n7474_2_pin2), .pin3(n7474_2_pin3), .pin4(n7474_2_pin1), .pin5(n7474_2_pin5),
    .pin6(n7474_2_pin2), .pin12(n7474_2_pin12), .pin11(n7474_2_pin5), .pin9(n7474_2_pin9),
    .pin8(n7474_2_pin12));  // open: pin13, pin10
  Button button_2 (.out(n7474_2_pin3));
  LED led_2 (.in(n7474_2_pin9));
  LED led_3 (.in(n7474_2_pin5));
  // also tied to VCC on the sheet: {n7474_1_pin1, n7474_2_pin1}
endmodule
