// Logisim project Example03.circ as structural Verilog: 1 circuit, main circuit main
module main (
  input  in_1,
  input  in_2,
  input  in_3,
  input  in_4,
  input  in_5,
  input  in_6,
  input  in_7,
  input  in_8,
  input  in_9,
  input  in_10,
  input  in_11,
  input  in_12
);

  wire nand_1_out, nand_2_out, nand_3_out, nand_4_out, nor_1_out, nor_2_out, not_1_out, not_2_out, not_3_out,
       not_4_out, not_5_out, not_6_out, not_7_out, not_8_out;

  not not_1 (not_1_out, in_4);
  not not_2 (not_2_out, in_5);
  not not_3 (not_3_out, in_10);
  not not_4 (not_4_out, in_11);
  nand nand_1 (nand_1_out, in_1, in_2, in_3);
  nand nand_2 (nand_2_out, not_1_out, not_2_out, in_6);
  nand nand_3 (nand_3_out, in_7, in_8, in_9);
  nand nand_4 (nand_4_out, not_3_out, not_4_out, in_12);
  not not_5 (not_5_out, nand_1_out);
  not not_6 (not_6_out, nand_2_out);
  not not_7 (not_7_out, not_5_out);
  not not_8 (not_8_out, not_6_out);
  nor nor_1 (nor_1_out, nand_3_out, nand_4_out);
  LED led_1 (.in(nor_1_out));
  nor nor_2 (nor_2_out, not_7_out, not_8_out);
  LED led_2 (.in(nor_2_out));
endmodule
