// Logisim project Exemplo5.circ as structural Verilog: 1 circuit, main circuit main
module main (
  input  in_1,
  input  in_2,
  input  in_3,
  input  in_4,
  input  in_5,
  input  in_6,
  input  A,
  input  B
);

  wire and_1_out, and_2_out, and_3_out, nand_1_out, nor_1_out, nor_2_out, not_1_out, not_2_out, not_3_out,
       not_4_out, not_5_out, not_6_out, not_7_out, or_1_out;

  not not_1 (not_1_out, in_1);
  not not_2 (not_2_out, in_2);
  not not_3 (not_3_out, in_6);
  nor nor_1 (nor_1_out, not_1_out, not_2_out, in_3);
  nor nor_2 (nor_2_out, in_4, in_5, not_3_out);
  not not_4 (not_4_out, A);
  not not_5 (not_5_out, nor_1_out);
  not not_6 (not_6_out, nor_2_out);
  not not_7 (not_7_out, B);
  nand nand_1 (nand_1_out, not_5_out, not_6_out);
  and and_1 (and_1_out, not_7_out, not_4_out);
  and and_2 (and_2_out, not_4_out, B);
  and and_3 (and_3_out, A, B);
  LED led_1 (.in(nand_1_out));
  or or_1 (or_1_out, and_1_out, and_2_out, and_3_out);
  LED Saida (.in(or_1_out));
endmodule
