// Logisim project FlipFlop_RS.circ as structural Verilog: 1 circuit, main circuit main
module main (
  input  S,
  input  Clock,
  input  R,
  input  in_4,
  input  in_5,
  input  in_6
);

  wire F1_out, F2_out, F3_out, F4_out, F5_out, F6_out, F7_out, F8_out, F9_out, s_r_ff_1_q, s_r_ff_1_qn;

  nand F1 (F1_out, S, Clock);
  nand F2 (F2_out, Clock, R);
  nand F3 (F3_out, F1_out, F4_out);
  nand F4 (F4_out, F3_out, F2_out);
  not F5 (F5_out, Clock);
  S_R_Flip_Flop s_r_ff_1 (.S(in_4), .R(in_5), .clk(in_6), .Q(s_r_ff_1_q), .Qn(s_r_ff_1_qn));  // open: reset, preset
  LED led_1 (.in(s_r_ff_1_q));
  LED led_2 (.in(s_r_ff_1_qn));
  nand F6 (F6_out, F3_out, F5_out);
  nand F7 (F7_out, F5_out, F4_out);
  nand F8 (F8_out, F6_out, F9_out);
  nand F9 (F9_out, F8_out, F7_out);
  LED Q (.in(F8_out));
  LED NOT_Q (.in(F9_out));

  // Notes on the sheet:
  //   Mestre
  //   Escravo
endmodule
