// Logisim project FlipFlop_jK.circ as structural Verilog: 1 circuit, main circuit main
module main (
  input  J,
  input  Clock,
  input  K,
  input  in_4,
  input  in_5,
  input  in_6
);

  wire F1_out, F2_out, F3_out, F4_out, F5_out, F6_out, F7_out, F8_out, F9_out, j_k_ff_1_q, j_k_ff_1_qn;

  nand F1 (F1_out, F9_out, J, Clock);
  nand F2 (F2_out, Clock, K, F8_out);
  J_K_Flip_Flop j_k_ff_1 (.J(in_4), .K(in_5), .clk(in_6), .Q(j_k_ff_1_q), .Qn(j_k_ff_1_qn));  // open: preset, reset
  nand F3 (F3_out, F1_out, F4_out);
  nand F4 (F4_out, F3_out, F2_out);
  not F5 (F5_out, Clock);
  LED led_1 (.in(j_k_ff_1_q));
  LED led_2 (.in(j_k_ff_1_qn));
  nand F6 (F6_out, F3_out, F5_out);
  nand F7 (F7_out, F5_out, F4_out);
  nand F8 (F8_out, F6_out, F9_out);
  nand F9 (F9_out, F8_out, F7_out);
  LED Q (.in(F8_out));
  LED NOT_Q (.in(F9_out));

  // Notes on the sheet:
  //   Mestre
  //   Escravo
endmodule
